# Fritzing sketch waterflowSchm (saved by Fritzing 0.9.2b)
circuit board: 8.52101cm x 5.88896cm
breadboards: 1

parts:
  red1 = LEDs [package=led10mm]
  yl1 = LEDs [package=led10mm]
  gr = LEDs [package=led10mm]
  yl2 = LEDs [package=led10mm]
  red2 = LEDs [package=led10mm]
  pwr = LEDs [package=led10mm]
  R6 = Resistor [tolerance=±5% resistance=220 package=THT]
  R1 = Resistor [tolerance=±5% resistance=220 package=THT]
  R2 = Resistor [tolerance=±5% resistance=220 package=THT]
  R3 = Resistor [tolerance=±5% resistance=220 package=THT]
  R4 = Resistor [tolerance=±5% resistance=220 package=THT]
  R5 = Resistor [tolerance=±5% resistance=220 package=THT]
  ArduinoMiniPro = Arduino Pro Mini v13
  J1 = Piezo Speaker
  JP2 = Header 3 [package=screwterminal-3.5mm-3_lock.007s]

nets:
  GND: red1.A, yl1.A, gr.A, yl2.A, red2.A, pwr.A, ArduinoMiniPro.GND, J1.pin1, JP2.3
  N1: red1.C, R1.Pin_1
  N2: yl1.C, R2.Pin_1
  N3: gr.C, R3.Pin_1
  N4: yl2.C, R4.Pin_1
  N5: red2.C, R5.Pin_1
  N6: pwr.C, R6.Pin_1
  N7: R6.Pin_0, ArduinoMiniPro.D8
  N8: R1.Pin_0, ArduinoMiniPro.D3_PWM
  N9: R2.Pin_0, ArduinoMiniPro.D4
  N10: R3.Pin_0, ArduinoMiniPro.D5_PWM
  N11: R4.Pin_0, ArduinoMiniPro.D6_PWM
  N12: R5.Pin_0, ArduinoMiniPro.D7
  N13: ArduinoMiniPro.VCC, JP2.2
  N14: ArduinoMiniPro.D12/MISO, J1.pin2
  N15: ArduinoMiniPro.D2, JP2.1
